# Fritzing sketch torreta (saved by Fritzing 0.9.3b)
breadboards: 1

parts:
  Componente1 = Arduino Uno (Rev3)
  J1 = Basic Servo
  HC-SR04_Sensor_1 = HC-SR04 Ultrasonic Distance Sensor
  J2 = Piezo Speaker
  C2 = Electrolytic Capacitor [capacitance=1µF package="100 mil [THT, electrolytic]"]  # not connected

nets:
  N1: Componente1.D9_PWM, HC-SR04_Sensor_1.ECHO
  N2: Componente1.D10_PWM/SS, HC-SR04_Sensor_1.TRIG
  GND: Componente1.GND, J1.gnd, HC-SR04_Sensor_1.GND, J2.pin1
  N3: Componente1.D3_PWM, J2.pin2
  N4: Componente1.D5_PWM, J1.pulse
  VCC: Componente1.5V, J1.vcc, HC-SR04_Sensor_1.VCC

// code stored in the sketch: torreta-1.0.0.ino
#include <math.h>

void setup() {  
	randomSeed(analogRead(0));
	Serial.begin(9600);
}

void loop() {
	int data = random(0,255);
	Serial.write(data); // data value must be 0-255
	delay(1000);
}
